// Logisim project 组合电路功能仿真.circ as structural Verilog: 1 circuit, main circuit Simulation
module Simulation (
);

  wire Clock, f1, f2, x1, x2, x3, x4;

  Clock #(.highDuration(1), .lowDuration(1)) clock_1 (.out(Clock));
  // Digital_Oscilloscope #(.nState(22), .frontlines("rising"), .showclock("true")) digital_oscilloscope_1: pin names not known; wires that end beside it: Clock, x1, x2, x3, x4, f1, f2
  Counter #(.width(4), .max('hf), .ongoal("wrap"), .trigger("rising"), .behavior("new")) counter_1 (
    .Q({x1, x2, x3, x4}), .clk(Clock));  // open: load, D, count, carry, clr, preset, down

  // Notes on the sheet:
  //   本案支持不超过4输入2输出的组合电路的功能仿真
  //   Ctrl+K自动仿真
  //   工程-->加载库-->Logisim库...，加入待测电路
endmodule
